# Fritzing sketch Diagram_extended (saved by Fritzing 0.9.3b)
circuit board: 8.46667cm x 5.64444cm

parts:
  U1 = NodeMCU V1.0
  5V = Power plug
  DotStar1 = DorStar LED Strip [part_number=2239]
  LED1 = LED - 3mm [color="Blue (430nm)" package="3 mm [THT]"]
  S1 = Momentary Switch [package=ksa_sealed_tac_switch]
  R1 = Resistor [tolerance=±5% resistance=470 package="0805 [SMD]"]
  R2 = Resistor [tolerance=±5% resistance=470 package="1206 [SMD]"]
  R3 = Resistor [tolerance=±5% resistance=470 package="1206 [SMD]"]
  FLASH = Momentary Switch [part_number=FLASH package=ksa_sealed_tac_switch]
  OLED_I2C1 = OLED 128x64 I2C Monochrome Display
  Composant1 = Adafruit MAX4466 Electret Microphone Amplifier [part_number="Adafruit #1063"]

nets:
  N1: U1.D1, OLED_I2C1.SCK
  N2: U1.D2, OLED_I2C1.SDA
  N3: U1.D3, R3.Pin_0
  N4: U1.D4, LED1.cathode, R1.Pin_0
  3V3: U1.3V3, LED1.anode, OLED_I2C1.VDD, Composant1.VCC
  GND: U1.GND, 5V.GND, DotStar1.GND, S1.1, FLASH.1, OLED_I2C1.GND, Composant1.GND
  N5: U1.D5, DotStar1.CI
  N6: U1.D7, DotStar1.DI
  VIN: U1.Vin, 5V.VCC, DotStar1.+5V
  N7: U1.RST, R2.Pin_1
  N8: U1.A0, Composant1.OUT
  N9: S1.3, R1.Pin_1, R2.Pin_0
  N10: R3.Pin_1, FLASH.3

custom parts:
  NodeMCU V1.0: ESP8266 based NodeMCU
  DorStar LED Strip: DotStar LED strip, black, 60 LEDs/m
  Adafruit MAX4466 Electret Microphone Amplifier: Add an ear to your project with this well-designed electret microphone amplifier. This fully assembled and tested board comes with a 20-20KHz electret microphone soldered on. For the amplification, we use the Maxim MAX4466, an op-amp specifically designed for this delicate task! The amplifier has excellent power supply noise rejection, so this amplifier sounds really good and isn't nearly as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
