# Fritzing sketch ESP MQTT Digital LEDs Wiring Diagram (saved by Fritzing 0.9.3b)

parts:
  U1 = NodeMCU V1.0
  5V = Power plug
  DotStar1 = DorStar LED Strip [part_number=2239]
  DotStar2 = DorStar LED Strip [part_number=2239]

nets:
  N1: U1.D5, DotStar1.CI
  N2: U1.D7, DotStar1.DI
  +5V: U1.Vin, 5V.VCC, DotStar1.+5V, DotStar2.+5V
  GND: U1.GND, 5V.GND, DotStar1.GND, DotStar2.GND
  N3: DotStar1.CO, DotStar2.CI
  N4: DotStar1.DO, DotStar2.DI

custom parts:
  NodeMCU V1.0: ESP8266 based NodeMCU
  DorStar LED Strip: DotStar LED strip, black, 60 LEDs/m
